// Logisim project 19CS020078085CLONE.circ as structural Verilog: 1 circuit, main circuit main
module main (
  input  [3:0] ADDRESSC,
  input  [3:0] ADDRESSB,
  input  [3:0] ADDRESSA,
  input  [3:0] OPCODE,
  input  [3:0] RAADDRESS,
  input  [3:0] RBADDRESS,
  input  [3:0] RCADDRESS,
  input  [15:0] IMMEDIATE,
  input  in_9,
  input  in_10,
  output [15:0] out_11
);

  wire ADD, ADI, AND, ANI, button_1_out, button_2_out, clktunnel, demultiplexer_1_out13, HLT, LOAD, MEMMUX,
       MOVE, MVI, OR, ORI, R1E, R2E, R3E, R4E, R5E, R6E, R7E, R8E, R9E, R10E, R11E, R12E, R13E, R14E, R15E,
       R16E, STORE, SUB, SUI;
  wire [15:0] bit_extender_1_out, IMMEDIATE_t, multiplexer_3_out;
  wire [15:12] MEMORYDATA;
  wire [31:0] BOTH, DIFF, INPUTTORGTF, MEMORYADDRESS, multiplexer_1_out, multiplexer_2_out,
       multiplexer_4_out, ORR, R1O, R2O, R3O, R4O, R5O, R6O, R7O, R8O, R9O, R10O, R11O, R12O, R13O, R14O,
       R15O, R16O, RAin, RB_q, RBin, RZin, SUM, undriven;

  Button button_1 (.out(button_1_out));
  Register #(.width(32)) RZ (.D(RZin), .Q(MEMORYADDRESS), .clk(clktunnel));  // open: en, clr
  Multiplexer #(.width(32)) multiplexer_1 (
    .in0(MEMORYADDRESS), .in1({IMMEDIATE_t, MEMORYDATA, MEMORYDATA, MEMORYDATA, OPCODE}),
    .out(multiplexer_1_out));  // open: sel, en
  Clock clk (.out(clktunnel));
  Register #(.width(32)) RY (.D(multiplexer_1_out), .Q(INPUTTORGTF), .clk(clktunnel));  // open: en, clr
  Demultiplexer #(.select(4)) demultiplexer_1 (
    .out0(MOVE), .out1(MVI), .out2(LOAD), .out3(STORE), .out4(ADD), .out5(ADI), .out6(SUB), .out7(SUI),
    .out8(AND), .out9(ANI), .out10(OR), .out11(ORI), .out12(HLT), .out13(demultiplexer_1_out13), .in(1'b1),
    .sel(OPCODE));  // open: out14, out15, en
  Register #(.width(32)) R1 (.D(INPUTTORGTF), .en(R1E), .Q(R1O), .clk(clktunnel), .clr(button_1_out));
  Register #(.width(32)) R9 (.D(INPUTTORGTF), .en(R9E), .Q(R9O), .clk(clktunnel), .clr(button_1_out));
  Multiplexer #(.select(4), .width(32)) multiplexer_2 (
    .in0(R1O), .in1(R2O), .in2(R3O), .in3(R4O), .in4(R5O), .in5(R6O), .in6(R7O), .in7(R8O), .in8(R9O),
    .in9(R10O), .in10(R11O), .in11(R12O), .in12(R13O), .in13(R14O), .in14(R15O), .in15(R16O),
    .out(multiplexer_2_out), .sel(ADDRESSA));  // open: en
  Register #(.width(32)) R2 (.D(INPUTTORGTF), .en(R2E), .Q(R2O), .clk(clktunnel), .clr(button_1_out));
  Register #(.width(32)) RA (.D(multiplexer_2_out), .Q(RAin), .clk(clktunnel));  // open: en, clr
  Register #(.width(32)) R10 (.D(INPUTTORGTF), .en(R10E), .Q(R10O), .clk(clktunnel), .clr(button_1_out));
  Register #(.width(32)) R3 (.D(INPUTTORGTF), .en(R3E), .Q(R3O), .clk(clktunnel), .clr(button_1_out));
  Register #(.width(32)) R11 (.D(INPUTTORGTF), .en(R11E), .Q(R11O), .clk(clktunnel), .clr(button_1_out));
  Bit_Extender #(.in_width(32)) bit_extender_1 (.in(MEMORYADDRESS), .out(bit_extender_1_out));
  Multiplexer #(.width(16)) multiplexer_3 (
    .in0(out_11), .in1(bit_extender_1_out), .out(multiplexer_3_out), .sel(MEMMUX));  // open: en
  Register #(.width(32)) R4 (.D(INPUTTORGTF), .en(R4E), .Q(R4O), .clk(clktunnel), .clr(button_1_out));
  Register #(.width(32)) R12 (.D(INPUTTORGTF), .en(R12E), .Q(R12O), .clk(clktunnel), .clr(button_1_out));
  RAM #(.addrWidth(16), .dataWidth(32)) ram_1 (
    .addr(multiplexer_3_out), .data({IMMEDIATE_t, MEMORYDATA, MEMORYDATA, MEMORYDATA, OPCODE}), .ld(in_9),
    .clr(in_10));  // open: sel, clk
  Register #(.width(32)) R5 (.D(INPUTTORGTF), .en(R5E), .Q(R5O), .clk(clktunnel), .clr(button_1_out));
  Register #(.width(32)) R13 (.D(INPUTTORGTF), .en(R13E), .Q(R13O), .clk(clktunnel), .clr(button_1_out));
  Register #(.width(32)) R6 (.D(INPUTTORGTF), .en(R6E), .Q(R6O), .clk(clktunnel), .clr(button_1_out));
  Register #(.width(32)) R14 (.D(INPUTTORGTF), .en(R14E), .Q(R14O), .clk(clktunnel), .clr(button_1_out));
  Multiplexer #(.select(4), .width(32)) multiplexer_4 (
    .in0(R1O), .in1(R2O), .in2(R3O), .in3(R4O), .in4(R5O), .in5(R6O), .in6(R7O), .in7(R8O), .in8(R9O),
    .in9(R10O), .in10(R11O), .in11(R12O), .in12(R13O), .in13(R14O), .in14(R15O), .in15(R16O),
    .out(multiplexer_4_out), .sel(ADDRESSB));  // open: en
  Register #(.width(32)) RB (.D(multiplexer_4_out), .Q(RB_q), .clk(clktunnel));  // open: en, clr
  Multiplexer #(.width(32)) multiplexer_5 (.in0(RB_q), .in1(undriven), .out(RBin));  // open: sel, en
  Register #(.width(32)) R7 (.D(INPUTTORGTF), .en(R7E), .clk(clktunnel), .clr(button_1_out));  // open: Q
  Register #(.width(32)) R15 (.D(INPUTTORGTF), .en(R15E), .Q(R15O), .clk(clktunnel), .clr(button_1_out));
  Bit_Extender #(.in_width(32)) bit_extender_2 (.in(undriven));  // open: out
  Register #(.width(32)) R8 (.D(INPUTTORGTF), .en(R8E), .clk(clktunnel), .clr(button_1_out));  // open: Q
  Register #(.width(32)) R16 (.D(INPUTTORGTF), .en(R16E), .Q(R16O), .clk(clktunnel), .clr(button_1_out));
  Counter #(.width(16), .max('hffff)) counter_1 (
    .Q(out_11), .clk(clktunnel), .clr(button_2_out));  // open: load, D, count, carry
  Demultiplexer #(.select(4)) demultiplexer_2 (
    .out0(R1E), .out1(R2E), .out2(R3E), .out3(R4E), .out4(R5E), .out5(R6E), .out6(R7E), .out7(R8E),
    .out8(R9E), .out9(R10E), .out10(R11E), .out11(R12E), .out12(R13E), .out13(R14E), .out14(R15E),
    .out15(R16E), .in(1'b1), .sel(ADDRESSC));  // open: en
  Button button_2 (.out(button_2_out));
  Subtractor #(.width(32)) subtractor_1 (.a(RAin), .b(RBin), .out(DIFF));  // open: bin, bout
  Demultiplexer #(.select(2), .width(32)) demultiplexer_3 (
    .out0(SUM), .out1(DIFF), .out2(BOTH), .out3(ORR), .in(RZin));  // open: sel, en
  Adder #(.width(32)) adder_1 (.a(RAin), .b(RBin), .out(SUM));  // open: cin, cout
  assign BOTH = RAin & RBin;  // AND_Gate and_1, 32 bits wide
  assign ORR = RAin | RBin;  // OR_Gate or_1, 32 bits wide
  // Probe on {IMMEDIATE, RCADDRESS, RBADDRESS, RAADDRESS, OPCODE}

  // Other names for the same wires on the sheet: MEMORYDATA (some bits) = {IMMEDIATE_t, MEMORYDATA, MEMORYDATA, OPCODE};
  //   RACODETUN[3:0] = MEMORYDATA; OPCODETUN[3:0] = OPCODE; PC[15:0] = out_11

  // Notes on the sheet:
  //   REGISTERFILE
  //   MEMORY
  //   CONTROLSIGNAL
  //   PC
  //   ALU
  //   HEXCONVERTOR
endmodule
